# Fritzing sketch mp3 (saved by Fritzing 0.9.2b)
breadboards: 1

parts:
  S1 = Pushbutton [package="[THT]"]
  LED1 = LED - 5mm [color="Red (633nm)" package="5 mm [THT]"]
  R1 = Resistor [tolerance=±5% resistance=220 package=THT]
  S2 = Pushbutton [package="[THT]"]
  S3 = Pushbutton [package="[THT]"]
  Raspberry_Pi2 = Raspberry Pi B+
  R2 = Resistor [tolerance=±5% resistance=220 package=THT]  # not connected

nets:
  N1: S1.Pin_1, S1.Pin_2, Raspberry_Pi2.GPIO18
  N2: S1.Pin_3, S1.Pin_4, R1.Pin_1, S2.Pin_3, S2.Pin_4, S3.Pin_3, S3.Pin_4, Raspberry_Pi2.GND
  N3: LED1.cathode, R1.Pin_0
  N4: LED1.anode, Raspberry_Pi2.GPIO4
  N5: S2.Pin_1, S2.Pin_2, Raspberry_Pi2.GPIO14
  N6: S3.Pin_1, S3.Pin_2, Raspberry_Pi2.GPIO15
